// Logisim project pongtron_5001.circ as structural Verilog: 18 circuits, main circuit main
module main (
);

  wire ballcollisionhandler_1_iscolliding, clock_1_out, IsNewGame, IsPaused, IsRunning,
       PlayerA_isballinpaddlerange, PlayerAIsComputer, PlayerAScores, PlayerB_isballinpaddlerange,
       PlayerBIsComputer, PlayerBScores, RunThisBastard;
  wire [1:0] BallStartDirection, PlayerAComputerLevel, PlayerAControl, PlayerBComputerLevel, PlayerBControl;
  wire [4:0] bit_extender_2_out, PlayerA_paddlepositiony, PlayerAPaddleSize, PlayerB_paddlepositiony,
       PlayerBPaddleSize;
  wire [5:0] bit_extender_1_out;
  wire [7:0] BallX, BallY;
  wire [15:0] PlayerAScore_score, PlayerBScore_score;
  wire [63:0] displaydriver_1_out_12, displaydriver_1_out_13, displaydriver_1_out_14, displaydriver_1_out_15,
       displaydriver_1_out_16, displaydriver_1_out_17, displaydriver_1_out_18, displaydriver_1_out_19,
       displaydriver_1_out_20, displaydriver_1_out_21, displaydriver_1_out_22, displaydriver_1_out_23,
       displaydriver_1_out_24, displaydriver_1_out_25, displaydriver_1_out_26, displaydriver_1_out_27,
       displaydriver_1_out_28, displaydriver_1_out_29, displaydriver_1_out_30, displaydriver_1_out_31,
       displaydriver_1_out_32, displaydriver_1_out_33, displaydriver_1_out_34, displaydriver_1_out_35;

  or or_1 (IsNewGame, PlayerAScores, PlayerBScores, RunThisBastard);
  Clock clock_1 (.out(clock_1_out));
  and and_1 (IsRunning, ~RunThisBastard, clock_1_out);  // AND_Gate
  BallHandler ballhandler_1 (
    .ForceFlipX(ballcollisionhandler_1_iscolliding), .Reset(IsNewGame), .PlayfieldCenterX(8'h18),
    .PlayfieldCenterY(8'h10), .LockMovement(IsPaused), .Clock(clock_1_out),
    .StartDirection(BallStartDirection), .BallX(BallX), .BallY(BallY));
  PlayerHandler PlayerA (
    .Clock(clock_1_out), .IsComputerPlayer(PlayerAIsComputer), .LockMovement(IsPaused),
    .ResetPaddleToCenter(RunThisBastard), .MovementDirection(PlayerAControl),
    .Difficulty(PlayerAComputerLevel), .PaddleSize(PlayerAPaddleSize), .BallY(BallY),
    .IsBallInPaddleRange(PlayerA_isballinpaddlerange), .PaddlePositionY(PlayerA_paddlepositiony));
  PlayerHandler PlayerB (
    .Clock(clock_1_out), .IsComputerPlayer(PlayerBIsComputer), .LockMovement(IsPaused),
    .ResetPaddleToCenter(RunThisBastard), .MovementDirection(PlayerBControl),
    .Difficulty(PlayerBComputerLevel), .PaddleSize(PlayerBPaddleSize), .BallY(BallY),
    .IsBallInPaddleRange(PlayerB_isballinpaddlerange), .PaddlePositionY(PlayerB_paddlepositiony));
  ScoreHandler PlayerAScore (
    .ClearScore(RunThisBastard), .LockScore(IsPaused), .Increment(PlayerAScores), .Score(PlayerAScore_score));
  ScoreHandler PlayerBScore (
    .ClearScore(RunThisBastard), .LockScore(IsPaused), .Increment(PlayerBScores), .Score(PlayerBScore_score));
  BallStartDirectionHandler ballstartdirectionhandler_1 (
    .ScoreA(PlayerAScore_score), .ScoreB(PlayerBScore_score), .Clock(clock_1_out), .IsNewGame(IsNewGame),
    .Reset(RunThisBastard), .BallStartDirection(BallStartDirection));
  BallCollisionHandler ballcollisionhandler_1 (
    .BallPositionX(BallX), .CanCollideWithPlayerA(PlayerA_isballinpaddlerange), .PlayerAPositionX({8{1'b0}}),
    .CanCollideWithPlayerB(PlayerB_isballinpaddlerange), .PlayerBPositionX(8'h2f), .PlayfieldCenterX(8'h18),
    .IsColliding(ballcollisionhandler_1_iscolliding), .IsOnLeftEdge(PlayerBScores),
    .IsOnRightEdge(PlayerAScores));
  Bit_Extender #(.out_width(6), .\type ("zero")) bit_extender_1 (.in(BallX), .out(bit_extender_1_out));
  Slider #(.width(2)) slider_1 (.out(PlayerAComputerLevel));
  Slider #(.width(5)) slider_2 (.out(PlayerAPaddleSize));
  Bit_Extender #(.out_width(5), .\type ("zero")) bit_extender_2 (.in(BallY), .out(bit_extender_2_out));
  Pull_Resistor pull_resistor_1 (.node(PlayerAIsComputer));
  // Switch switch_1: pin names not known; wires that end beside it: PlayerAIsComputer, 1'b1
  Button AUp (.out(PlayerAControl[0]));
  Button ADown (.out(PlayerAControl[1]));
  DisplayDriver displaydriver_1 (
    .PaddleAPositionY(PlayerA_paddlepositiony), .PaddleASize(PlayerAPaddleSize), .BallY(bit_extender_2_out),
    .BallX(bit_extender_1_out), .IsPaused(IsPaused), .ScorePositionY(5'b10111),
    .PauseScreenPositionY(5'b01011), .ScoreA(PlayerAScore_score), .PaddleBPositionY(PlayerB_paddlepositiony),
    .PaddleBSize(PlayerBPaddleSize), .ScoreB(PlayerBScore_score), .out_12(displaydriver_1_out_12),
    .out_13(displaydriver_1_out_13), .out_14(displaydriver_1_out_14), .out_15(displaydriver_1_out_15),
    .out_16(displaydriver_1_out_16), .out_17(displaydriver_1_out_17), .out_18(displaydriver_1_out_18),
    .out_19(displaydriver_1_out_19), .out_20(displaydriver_1_out_20), .out_21(displaydriver_1_out_21),
    .out_22(displaydriver_1_out_22), .out_23(displaydriver_1_out_23), .out_24(displaydriver_1_out_24),
    .out_25(displaydriver_1_out_25), .out_26(displaydriver_1_out_26), .out_27(displaydriver_1_out_27),
    .out_28(displaydriver_1_out_28), .out_29(displaydriver_1_out_29), .out_30(displaydriver_1_out_30),
    .out_31(displaydriver_1_out_31), .out_32(displaydriver_1_out_32), .out_33(displaydriver_1_out_33),
    .out_34(displaydriver_1_out_34), .out_35(displaydriver_1_out_35));
  Pull_Resistor pull_resistor_2 (.node(IsPaused));
  // Switch Pause: pin names not known; wires that end beside it: IsPaused, 1'b1
  DotMatrix #(.matrixcols(48), .matrixrows(32)) dotmatrix_1 (
    .col0(displaydriver_1_out_12[31:0]), .col1(displaydriver_1_out_12[63:32]),
    .col2(displaydriver_1_out_13[31:0]), .col3(displaydriver_1_out_13[63:32]),
    .col4(displaydriver_1_out_14[31:0]), .col5(displaydriver_1_out_14[63:32]),
    .col6(displaydriver_1_out_15[31:0]), .col7(displaydriver_1_out_15[63:32]),
    .col8(displaydriver_1_out_16[31:0]), .col9(displaydriver_1_out_16[63:32]),
    .col10(displaydriver_1_out_17[31:0]), .col11(displaydriver_1_out_17[63:32]),
    .col12(displaydriver_1_out_18[31:0]), .col13(displaydriver_1_out_18[63:32]),
    .col14(displaydriver_1_out_19[31:0]), .col15(displaydriver_1_out_19[63:32]),
    .col16(displaydriver_1_out_20[31:0]), .col17(displaydriver_1_out_20[63:32]),
    .col18(displaydriver_1_out_21[31:0]), .col19(displaydriver_1_out_21[63:32]),
    .col20(displaydriver_1_out_22[31:0]), .col21(displaydriver_1_out_22[63:32]),
    .col22(displaydriver_1_out_23[31:0]), .col23(displaydriver_1_out_23[63:32]),
    .col24(displaydriver_1_out_24[31:0]), .col25(displaydriver_1_out_24[63:32]),
    .col26(displaydriver_1_out_25[31:0]), .col27(displaydriver_1_out_25[63:32]),
    .col28(displaydriver_1_out_26[31:0]), .col29(displaydriver_1_out_26[63:32]),
    .col30(displaydriver_1_out_27[31:0]), .col31(displaydriver_1_out_27[63:32]),
    .col32(displaydriver_1_out_28[31:0]), .col33(displaydriver_1_out_28[63:32]),
    .col34(displaydriver_1_out_29[31:0]), .col35(displaydriver_1_out_29[63:32]),
    .col36(displaydriver_1_out_30[31:0]), .col37(displaydriver_1_out_30[63:32]),
    .col38(displaydriver_1_out_31[31:0]), .col39(displaydriver_1_out_31[63:32]),
    .col40(displaydriver_1_out_32[31:0]), .col41(displaydriver_1_out_32[63:32]),
    .col42(displaydriver_1_out_33[31:0]), .col43(displaydriver_1_out_33[63:32]),
    .col44(displaydriver_1_out_34[31:0]), .col45(displaydriver_1_out_34[63:32]),
    .col46(displaydriver_1_out_35[31:0]), .col47(displaydriver_1_out_35[63:32]));
  Pull_Resistor #(.pull(1)) pull_resistor_3 (.node(RunThisBastard));
  // Switch Run: pin names not known; wires that end beside it: RunThisBastard, 1'b0
  LED led_1 (.in(IsRunning));
  // Switch switch_2: pin names not known; wires that end beside it: 1'b1, PlayerBIsComputer
  Button BUp (.out(PlayerBControl[0]));
  Button BDown (.out(PlayerBControl[1]));
  Pull_Resistor pull_resistor_4 (.node(PlayerBIsComputer));
  Slider #(.width(2)) slider_3 (.out(PlayerBComputerLevel));
  Slider #(.width(5)) slider_4 (.out(PlayerBPaddleSize));

  // Other names for the same wires on the sheet: LockUpdates = IsPaused

  // Notes on the sheet:
  //   Player A
  //   Player B
endmodule

module ToDigit (
  input  [15:0] Number,
  output [3:0] Digit,
  output [15:0] Rest
);

  wire [11:0] divider_1_rem;

  Divider #(.width(16)) divider_1 (.a(Number), .b(16'ha), .out(Rest), .rem({divider_1_rem, Digit}));  // open: upper
endmodule

module BCDConverter (
  input  [15:0] Number,
  output [3:0] Digit_1x,
  output [3:0] Digit_10x,
  output [3:0] Digit_100x,
  output [3:0] Digit_1000x,
  output [3:0] Digit_100000x,
  output [19:0] BCD
);

  wire [15:0] todigit_1_rest, todigit_2_rest, todigit_3_rest, todigit_4_rest;

  ToDigit todigit_1 (.Number(Number), .Digit(BCD[3:0]), .Rest(todigit_1_rest));
  ToDigit todigit_2 (.Number(todigit_1_rest), .Digit(BCD[7:4]), .Rest(todigit_2_rest));
  ToDigit todigit_3 (.Number(todigit_2_rest), .Digit(BCD[11:8]), .Rest(todigit_3_rest));
  ToDigit todigit_4 (.Number(todigit_3_rest), .Digit(BCD[15:12]), .Rest(todigit_4_rest));
  ToDigit todigit_5 (.Number(todigit_4_rest), .Digit(BCD[19:16]));  // open: Rest

  assign Digit_1x = BCD[3:0];
  assign Digit_10x = BCD[7:4];
  assign Digit_100x = BCD[11:8];
  assign Digit_1000x = BCD[15:12];
  assign Digit_100000x = BCD[19:16];
endmodule

module PaddleHandler (
  input  LockMovement,
  input  [4:0] PaddleSize,
  input  ResetPosition,
  input  Clock,
  input  [1:0] Direction,
  input  [7:0] BallY,
  output [4:0] PaddlePositionY,
  output IsInPaddleRange
);

  wire and_1_out, and_2_out, and_3_out, CanKeepMovingUp, comparator_1_gt, comparator_2_lt, not_1_out,
       or_1_out, or_2_out, subtractor_2_bout;
  wire [3:0] bit_extender_2_out;
  wire [4:0] adder_2_out, adder_4_out, bit_extender_1_out, multiplier_1_out, PaddleY_q, subtractor_1_out,
       subtractor_3_out;

  not not_1 (not_1_out, LockMovement);
  and and_1 (and_1_out, Direction[0], Direction[1]);
  or or_1 (or_1_out, Direction[0], Direction[1]);
  and and_2 (and_2_out, not_1_out, or_1_out);
  Multiplier #(.width(5)) multiplier_1 (.a(5'b00010), .b(PaddleSize), .out(multiplier_1_out));  // open: cin, cout
  Counter #(.max('h1f), .ongoal("stay"), .width(5)) PaddleY (
    .load(or_2_out), .up(and_3_out), .count(and_2_out), .clk(Clock), .D(subtractor_1_out), .Q(PaddleY_q));  // open: clr, carry
  or or_2 (or_2_out, ResetPosition, and_1_out);
  and and_3 (and_3_out, Direction[0], ~CanKeepMovingUp);  // AND_Gate
  Subtractor #(.width(5)) subtractor_1 (.a(5'b10000), .b(PaddleSize), .out(subtractor_1_out));  // open: bin, bout
  Adder #(.width(5)) adder_1 (.a(PaddleY_q), .b(multiplier_1_out), .cout(CanKeepMovingUp));  // open: out, cin
  Subtractor #(.width(5)) subtractor_2 (
    .a(PaddleY_q), .b(multiplier_1_out), .bout(subtractor_2_bout));  // open: out, bin
  Adder #(.width(5)) adder_2 (.a(5'b00001), .b(PaddleSize), .out(adder_2_out));  // open: cin, cout
  Bit_Extender #(.out_width(5), .\type ("zero")) bit_extender_1 (.in(BallY), .out(bit_extender_1_out));
  Bit_Extender #(.out_width(4), .\type ("zero")) bit_extender_2 (.in(BallY), .out(bit_extender_2_out));
  Adder #(.width(5)) adder_3 (.a(PaddleSize), .b(PaddleY_q), .out(PaddlePositionY));  // open: cin, cout
  Adder #(.width(5)) adder_4 (.a(PaddlePositionY), .b(adder_2_out), .out(adder_4_out));  // open: cin, cout
  Subtractor #(.width(5)) subtractor_3 (
    .a(PaddlePositionY), .b(adder_2_out), .out(subtractor_3_out));  // open: bin, bout
  Hex_Digit_Display hex_digit_display_1 (.value(bit_extender_2_out));  // open: dp
  Comparator #(.mode("unsigned"), .width(5)) comparator_1 (
    .a(adder_4_out), .b(bit_extender_1_out), .gt(comparator_1_gt));  // open: eq, lt
  Comparator #(.mode("unsigned"), .width(5)) comparator_2 (
    .a(subtractor_3_out), .b(bit_extender_1_out), .lt(comparator_2_lt));  // open: gt, eq
  and and_4 (IsInPaddleRange, comparator_1_gt, comparator_2_lt);
endmodule

module BallHandler (
  input  ForceFlipX,
  input  Reset,
  input  [7:0] PlayfieldCenterX,
  input  [7:0] PlayfieldCenterY,
  input  LockMovement,
  input  Clock,
  input  [1:0] StartDirection,
  output [7:0] BallX,
  output [7:0] BallY
);

  wire comparator_1_eq, comparator_1_gt, comparator_2_eq, comparator_2_gt, demultiplexer_1_out0,
       demultiplexer_1_out1, demultiplexer_2_out0, demultiplexer_2_out1, FlipX, FlipY, MoveX_carry,
       MoveY_carry, not_1_out, not_3_out, not_4_out, or_1_out, or_2_out, or_3_out, or_4_out, t_ff_1_q,
       t_ff_2_q;
  wire [1:0] not_2_out;
  wire [7:0] multiplier_1_out, multiplier_2_out, subtractor_1_out, subtractor_2_out;

  not not_1 (not_1_out, LockMovement);
  Counter #(.ongoal("stay")) MoveX (
    .load(Reset), .up(FlipX), .count(not_1_out), .clk(Clock), .D(PlayfieldCenterX), .carry(MoveX_carry),
    .Q(BallX));  // open: clr
  Counter #(.ongoal("stay")) MoveY (
    .load(Reset), .up(FlipY), .count(not_1_out), .clk(Clock), .D(PlayfieldCenterY), .carry(MoveY_carry),
    .Q(BallY));  // open: clr
  Multiplier multiplier_1 (.a(PlayfieldCenterX), .b(8'h2), .out(multiplier_1_out));  // open: cin, cout
  Multiplier multiplier_2 (.a(PlayfieldCenterY), .b(8'h2), .out(multiplier_2_out));  // open: cin, cout
  Subtractor subtractor_1 (.a(multiplier_1_out), .b(8'h1), .out(subtractor_1_out));  // open: bin, bout
  Subtractor subtractor_2 (.a(multiplier_2_out), .b(8'h1), .out(subtractor_2_out));  // open: bin, bout
  or or_1 (or_1_out, ForceFlipX, comparator_1_gt, comparator_1_eq);
  Comparator #(.mode("unsigned")) comparator_1 (
    .a(BallX), .b(subtractor_1_out), .gt(comparator_1_gt), .eq(comparator_1_eq));  // open: lt
  Comparator #(.mode("unsigned")) comparator_2 (
    .a(BallY), .b(subtractor_2_out), .gt(comparator_2_gt), .eq(comparator_2_eq));  // open: lt
  or or_2 (or_2_out, comparator_2_eq, comparator_2_gt);
  assign not_2_out = ~StartDirection;  // NOT_Gate not_2, 2 bits wide
  or or_3 (or_3_out, or_1_out, MoveX_carry);
  or or_4 (or_4_out, or_2_out, MoveY_carry);
  Demultiplexer demultiplexer_1 (
    .out0(demultiplexer_1_out0), .out1(demultiplexer_1_out1), .in(Reset), .sel(not_2_out[0]));
  not not_3 (not_3_out, t_ff_1_q);
  T_Flip_Flop t_ff_1 (
    .T(or_3_out), .clk(Clock), .Q(t_ff_1_q), .reset(demultiplexer_1_out1), .preset(demultiplexer_1_out0));  // open: Qn
  T_Flip_Flop t_ff_2 (
    .T(or_4_out), .clk(Clock), .Q(t_ff_2_q), .reset(demultiplexer_2_out1), .preset(demultiplexer_2_out0));  // open: Qn
  not not_4 (not_4_out, t_ff_2_q);
  Demultiplexer demultiplexer_2 (
    .out0(demultiplexer_2_out0), .out1(demultiplexer_2_out1), .in(Reset), .sel(not_2_out[1]));
  Multiplexer multiplexer_1 (.in0(t_ff_1_q), .in1(not_3_out), .out(FlipX), .sel(or_1_out));
  Multiplexer multiplexer_2 (.in0(t_ff_2_q), .in1(not_4_out), .out(FlipY), .sel(or_2_out));

  // Notes on the sheet:
  //   ↓ Gambiarra-Oriented Design ↓
endmodule

module ComputerEnemyMovementHandler (
  input  [7:0] BallY,
  input  [7:0] PaddlePositionY,
  input  Clock,
  input  LockMovement,
  input  [1:0] Difficulty,
  output [1:0] Movement
);

  wire MoveEnabler_carry, not_1_out;
  wire [1:0] comparator_1_gt;

  not not_1 (not_1_out, LockMovement);
  Counter #(.max('h3), .ongoal("load"), .width(2)) MoveEnabler (
    .load(1'b0), .up(1'b1), .count(not_1_out), .clk(Clock), .D(Difficulty), .carry(MoveEnabler_carry));  // open: clr, Q
  Comparator #(.mode("unsigned")) comparator_1 (
    .a(BallY), .b(PaddlePositionY), .gt(comparator_1_gt[0]), .lt(comparator_1_gt[1]));  // open: eq
  Multiplexer #(.width(2)) multiplexer_1 (.in0(2'b00), .in1(comparator_1_gt), .out(Movement), .sel(MoveEnabler_carry));
endmodule

module DisplayDriver (
  input  [4:0] PaddleAPositionY,
  input  [4:0] PaddleASize,
  input  [4:0] BallY,
  input  [5:0] BallX,
  input  IsPaused,
  input  [4:0] ScorePositionY,
  input  [4:0] PauseScreenPositionY,
  input  [15:0] ScoreA,
  input  [4:0] PaddleBPositionY,
  input  [4:0] PaddleBSize,
  input  [15:0] ScoreB,
  output [63:0] out_12,
  output [63:0] out_13,
  output [63:0] out_14,
  output [63:0] out_15,
  output [63:0] out_16,
  output [63:0] out_17,
  output [63:0] out_18,
  output [63:0] out_19,
  output [63:0] out_20,
  output [63:0] out_21,
  output [63:0] out_22,
  output [63:0] out_23,
  output [63:0] out_24,
  output [63:0] out_25,
  output [63:0] out_26,
  output [63:0] out_27,
  output [63:0] out_28,
  output [63:0] out_29,
  output [63:0] out_30,
  output [63:0] out_31,
  output [63:0] out_32,
  output [63:0] out_33,
  output [63:0] out_34,
  output [63:0] out_35
);

  wire [31:0] PaddleA_paddledisplay, PaddleB_paddledisplay, scoredisplayhandler_1_out_3,
       scoredisplayhandler_1_out_4, scoredisplayhandler_1_out_5, scoredisplayhandler_1_out_6,
       scoredisplayhandler_1_out_7, scoredisplayhandler_1_out_8, scoredisplayhandler_1_out_9,
       scoredisplayhandler_1_out_10, scoredisplayhandler_1_out_11, scoredisplayhandler_1_out_12,
       scoredisplayhandler_1_out_13, scoredisplayhandler_1_out_14, scoredisplayhandler_2_out_3,
       scoredisplayhandler_2_out_4, scoredisplayhandler_2_out_5, scoredisplayhandler_2_out_6,
       scoredisplayhandler_2_out_7, scoredisplayhandler_2_out_8, scoredisplayhandler_2_out_9,
       scoredisplayhandler_2_out_10, scoredisplayhandler_2_out_11, scoredisplayhandler_2_out_12,
       scoredisplayhandler_2_out_13, scoredisplayhandler_2_out_14;
  wire [63:0] Ball_out_3, Ball_out_5, Ball_out_6, Ball_out_8, Ball_out_9, Ball_out_10, Ball_out_11,
       Ball_out_12, Ball_out_13, Ball_out_14, Ball_out_15, Ball_out_16, Ball_out_17, Ball_out_18,
       Ball_out_19, Ball_out_20, Ball_out_21, Ball_out_23, Ball_out_24, Ball_out_26, or_6_out, or_7_out,
       or_8_out, or_9_out, or_10_out, or_11_out, or_15_out, or_16_out;

  PaddleDisplayHandler PaddleA (
    .PaddlePositionY(PaddleAPositionY), .PaddleSize(PaddleASize), .PaddleDisplay(PaddleA_paddledisplay));
  BallDisplayHandler Ball (
    .BallY(BallY), .BallX(BallX), .out_3(Ball_out_3), .out_4(out_13), .out_5(Ball_out_5), .out_6(Ball_out_6),
    .out_7(out_16), .out_8(Ball_out_8), .out_9(Ball_out_9), .out_10(Ball_out_10), .out_11(Ball_out_11),
    .out_12(Ball_out_12), .out_13(Ball_out_13), .out_14(Ball_out_14), .out_15(Ball_out_15),
    .out_16(Ball_out_16), .out_17(Ball_out_17), .out_18(Ball_out_18), .out_19(Ball_out_19),
    .out_20(Ball_out_20), .out_21(Ball_out_21), .out_22(out_31), .out_23(Ball_out_23), .out_24(Ball_out_24),
    .out_25(out_34), .out_26(Ball_out_26));
  PaddleDisplayHandler PaddleB (
    .PaddlePositionY(PaddleBPositionY), .PaddleSize(PaddleBSize), .PaddleDisplay(PaddleB_paddledisplay));
  assign out_12 = {{32{1'b0}}, PaddleA_paddledisplay} | Ball_out_3;  // OR_Gate or_1, 64 bits wide
  assign out_35 = Ball_out_26 | {PaddleB_paddledisplay, {32{1'b0}}};  // OR_Gate or_2, 64 bits wide
  ScoreDisplayHandler scoredisplayhandler_1 (
    .ScorePositionY(ScorePositionY), .Score(ScoreA), .out_3(scoredisplayhandler_1_out_3),
    .out_4(scoredisplayhandler_1_out_4), .out_5(scoredisplayhandler_1_out_5),
    .out_6(scoredisplayhandler_1_out_6), .out_7(scoredisplayhandler_1_out_7),
    .out_8(scoredisplayhandler_1_out_8), .out_9(scoredisplayhandler_1_out_9),
    .out_10(scoredisplayhandler_1_out_10), .out_11(scoredisplayhandler_1_out_11),
    .out_12(scoredisplayhandler_1_out_12), .out_13(scoredisplayhandler_1_out_13),
    .out_14(scoredisplayhandler_1_out_14));
  ScoreDisplayHandler scoredisplayhandler_2 (
    .ScorePositionY(ScorePositionY), .Score(ScoreB), .out_3(scoredisplayhandler_2_out_3),
    .out_4(scoredisplayhandler_2_out_4), .out_5(scoredisplayhandler_2_out_5),
    .out_6(scoredisplayhandler_2_out_6), .out_7(scoredisplayhandler_2_out_7),
    .out_8(scoredisplayhandler_2_out_8), .out_9(scoredisplayhandler_2_out_9),
    .out_10(scoredisplayhandler_2_out_10), .out_11(scoredisplayhandler_2_out_11),
    .out_12(scoredisplayhandler_2_out_12), .out_13(scoredisplayhandler_2_out_13),
    .out_14(scoredisplayhandler_2_out_14));
  assign out_14 = {scoredisplayhandler_1_out_4, scoredisplayhandler_1_out_3} | Ball_out_5;  // OR_Gate or_3, 64 bits wide
  assign out_15 = {scoredisplayhandler_1_out_6, scoredisplayhandler_1_out_5} | Ball_out_6;  // OR_Gate or_4, 64 bits wide
  assign out_17 = {scoredisplayhandler_1_out_8, scoredisplayhandler_1_out_7} | Ball_out_8;  // OR_Gate or_5, 64 bits wide
  assign or_6_out = {scoredisplayhandler_1_out_10, scoredisplayhandler_1_out_9} | Ball_out_9;  // OR_Gate or_6, 64 bits wide
  assign or_7_out = {scoredisplayhandler_1_out_12, scoredisplayhandler_1_out_11} | Ball_out_11;  // OR_Gate or_7, 64 bits wide
  assign or_8_out = {scoredisplayhandler_1_out_14, scoredisplayhandler_1_out_13} | Ball_out_12;  // OR_Gate or_8, 64 bits wide
  assign or_9_out = {scoredisplayhandler_2_out_4, scoredisplayhandler_2_out_3} | Ball_out_17;  // OR_Gate or_9, 64 bits wide
  assign or_10_out = {scoredisplayhandler_2_out_6, scoredisplayhandler_2_out_5} | Ball_out_18;  // OR_Gate or_10, 64 bits wide
  assign or_11_out = {scoredisplayhandler_2_out_8, scoredisplayhandler_2_out_7} | Ball_out_20;  // OR_Gate or_11, 64 bits wide
  assign out_30 = {scoredisplayhandler_2_out_10, scoredisplayhandler_2_out_9} | Ball_out_21;  // OR_Gate or_12, 64 bits wide
  assign out_32 = {scoredisplayhandler_2_out_12, scoredisplayhandler_2_out_11} | Ball_out_23;  // OR_Gate or_13, 64 bits wide
  assign out_33 = {scoredisplayhandler_2_out_14, scoredisplayhandler_2_out_13} | Ball_out_24;  // OR_Gate or_14, 64 bits wide
  assign or_15_out = Ball_out_14 | 64'h3246624c00000000;  // OR_Gate or_15, 64 bits wide
  assign or_16_out = Ball_out_15 | 64'h2643c264;  // OR_Gate or_16, 64 bits wide
  PauseScreenHandler pausescreenhandler_1 (
    .Enable(IsPaused), .PausePositionY(PauseScreenPositionY), .in_3(or_6_out), .in_4(Ball_out_10),
    .in_5(or_7_out), .in_6(or_8_out), .in_7(Ball_out_13), .in_8(or_15_out), .in_9(or_16_out),
    .in_10(Ball_out_16), .in_11(or_9_out), .in_12(or_10_out), .in_13(Ball_out_19), .in_14(or_11_out),
    .out_15(out_18), .out_16(out_19), .out_17(out_20), .out_18(out_21), .out_19(out_22), .out_20(out_23),
    .out_21(out_24), .out_22(out_25), .out_23(out_26), .out_24(out_27), .out_25(out_28), .out_26(out_29));
  DotMatrix #(.matrixcols(48), .matrixrows(32)) dotmatrix_1 (
    .col0(out_12[31:0]), .col1(out_12[63:32]), .col2(out_13[31:0]), .col3(out_13[63:32]),
    .col4(out_14[31:0]), .col5(out_14[63:32]), .col6(out_15[31:0]), .col7(out_15[63:32]),
    .col8(out_16[31:0]), .col9(out_16[63:32]), .col10(out_17[31:0]), .col11(out_17[63:32]),
    .col12(out_18[31:0]), .col13(out_18[63:32]), .col14(out_19[31:0]), .col15(out_19[63:32]),
    .col16(out_20[31:0]), .col17(out_20[63:32]), .col18(out_21[31:0]), .col19(out_21[63:32]),
    .col20(out_22[31:0]), .col21(out_22[63:32]), .col22(out_23[31:0]), .col23(out_23[63:32]),
    .col24(out_24[31:0]), .col25(out_24[63:32]), .col26(out_25[31:0]), .col27(out_25[63:32]),
    .col28(out_26[31:0]), .col29(out_26[63:32]), .col30(out_27[31:0]), .col31(out_27[63:32]),
    .col32(out_28[31:0]), .col33(out_28[63:32]), .col34(out_29[31:0]), .col35(out_29[63:32]),
    .col36(out_30[31:0]), .col37(out_30[63:32]), .col38(out_31[31:0]), .col39(out_31[63:32]),
    .col40(out_32[31:0]), .col41(out_32[63:32]), .col42(out_33[31:0]), .col43(out_33[63:32]),
    .col44(out_34[31:0]), .col45(out_34[63:32]), .col46(out_35[31:0]), .col47(out_35[63:32]));
endmodule

module PaddleDisplayHandler (
  input  [4:0] PaddlePositionY,
  input  [4:0] PaddleSize,
  output [31:0] PaddleDisplay
);

  wire [4:0] multiplier_1_out, subtractor_1_out;
  wire [31:0] rom_1_data;

  ROM #(.addrWidth(5), .dataWidth(32)) rom_1 (.addr(multiplier_1_out), .data(rom_1_data));
  Multiplier #(.width(5)) multiplier_1 (.a(PaddleSize), .b(5'b00010), .out(multiplier_1_out));  // open: cin, cout
  Subtractor #(.width(5)) subtractor_1 (
    .a(PaddlePositionY), .b(PaddleSize), .out(subtractor_1_out));  // open: bin, bout
  Shifter #(.width(32)) shifter_1 (.in(rom_1_data), .\dist (subtractor_1_out), .out(PaddleDisplay));

  // Notes on the sheet:
  //   contents of rom_1 (hex, n*v repeats v):
  //   1 3 7 f 1f 3f 7f ff 1ff 3ff 7ff fff 1fff 3fff 7fff ffff 1ffff 3ffff 7ffff fffff 1fffff 3fffff 7fffff
  //   ffffff 1ffffff 3ffffff 7ffffff fffffff 1fffffff 3fffffff 7fffffff ffffffff
endmodule

module BallDisplayHandler (
  input  [4:0] BallY,
  input  [5:0] BallX,
  output [63:0] out_3,
  output [63:0] out_4,
  output [63:0] out_5,
  output [63:0] out_6,
  output [63:0] out_7,
  output [63:0] out_8,
  output [63:0] out_9,
  output [63:0] out_10,
  output [63:0] out_11,
  output [63:0] out_12,
  output [63:0] out_13,
  output [63:0] out_14,
  output [63:0] out_15,
  output [63:0] out_16,
  output [63:0] out_17,
  output [63:0] out_18,
  output [63:0] out_19,
  output [63:0] out_20,
  output [63:0] out_21,
  output [63:0] out_22,
  output [63:0] out_23,
  output [63:0] out_24,
  output [63:0] out_25,
  output [63:0] out_26
);

  wire [5:0] and_1_out, multiplexer_1_out, shifter_2_out;
  wire [63:0] shifter_1_out, shifter_3_out;

  assign and_1_out = BallX & 6'b000001;  // AND_Gate and_1, 6 bits wide
  Shifter #(.width(64)) shifter_1 (.in(64'h1), .\dist ({1'b0, BallY}), .out(shifter_1_out));
  Multiplexer #(.width(6)) multiplexer_1 (
    .in0({6{1'b0}}), .in1(6'b100000), .out(multiplexer_1_out), .sel(and_1_out[0]));
  Shifter #(.shift("lr"), .width(6)) shifter_2 (.in(BallX), .\dist (3'b001), .out(shifter_2_out));
  Shifter #(.width(64)) shifter_3 (.in(shifter_1_out), .\dist (multiplexer_1_out), .out(shifter_3_out));
  Demultiplexer #(.select(5), .width(64)) demultiplexer_1 (
    .out0(out_3), .out1(out_4), .out2(out_5), .out3(out_6), .out4(out_7), .out5(out_8), .out6(out_9),
    .out7(out_10), .out8(out_11), .out9(out_12), .out10(out_13), .out11(out_14), .out12(out_15),
    .out13(out_16), .out14(out_17), .out15(out_18), .out16(out_19), .out17(out_20), .out18(out_21),
    .out19(out_22), .out20(out_23), .out21(out_24), .out22(out_25), .out23(out_26), .in(shifter_3_out),
    .sel(shifter_2_out[4:0]));  // open: out24, out25, out26, out27, out28, out29, out30, out31
endmodule

module ScoreDisplayHandler (
  input  [4:0] ScorePositionY,
  input  [15:0] Score,
  output [31:0] out_3,
  output [31:0] out_4,
  output [31:0] out_5,
  output [31:0] out_6,
  output [31:0] out_7,
  output [31:0] out_8,
  output [31:0] out_9,
  output [31:0] out_10,
  output [31:0] out_11,
  output [31:0] out_12,
  output [31:0] out_13,
  output [31:0] out_14
);

  wire [3:0] bcdconverter_1_digit_1x, bcdconverter_1_digit_10x, bcdconverter_1_digit_100x;
  wire [4:0] bit_extender_1_out, bit_extender_2_out, bit_extender_3_out;

  BCDConverter bcdconverter_1 (
    .Number(Score), .Digit_1x(bcdconverter_1_digit_1x), .Digit_10x(bcdconverter_1_digit_10x),
    .Digit_100x(bcdconverter_1_digit_100x));  // open: Digit_1000x, Digit_100000x, BCD
  assign bit_extender_1_out = {{1{1'b0}}, bcdconverter_1_digit_100x};  // Bit_Extender bit_extender_1
  assign bit_extender_2_out = {{1{1'b0}}, bcdconverter_1_digit_10x};  // Bit_Extender bit_extender_2
  assign bit_extender_3_out = {{1{1'b0}}, bcdconverter_1_digit_1x};  // Bit_Extender bit_extender_3
  CharacterDisplayHandler characterdisplayhandler_1 (
    .CharacterPositionY(ScorePositionY), .Character(bit_extender_1_out), .out_3(out_3), .out_4(out_4),
    .out_5(out_5), .out_6(out_6));
  CharacterDisplayHandler characterdisplayhandler_2 (
    .CharacterPositionY(ScorePositionY), .Character(bit_extender_2_out), .out_3(out_7), .out_4(out_8),
    .out_5(out_9), .out_6(out_10));
  CharacterDisplayHandler characterdisplayhandler_3 (
    .CharacterPositionY(ScorePositionY), .Character(bit_extender_3_out), .out_3(out_11), .out_4(out_12),
    .out_5(out_13), .out_6(out_14));
endmodule

module CharacterROM (
  input  [4:0] Character,
  output [7:0] out_2,
  output [7:0] out_3,
  output [7:0] out_4,
  output [7:0] out_5
);

  ROM #(.addrWidth(5), .dataWidth(32)) rom_1 (.addr(Character), .data({out_5, out_4, out_3, out_2}));
  DotMatrix #(.matrixcols(4), .matrixrows(8)) dotmatrix_1 (.col0(out_2), .col1(out_3), .col2(out_4), .col3(out_5));

  // Notes on the sheet:
  //   contents of rom_1 (hex, n*v repeats v):
  //   7ef3cf7e 3ffff43 73fbcf67 66ffdb42 ffff6838 cedfdbfa 4edfdb7e 70fccfc3 66dffb76 7effdb72 7fffc87f
  //   6699ffff 66c3ff7e 7ec3ffff 5adbffff d0d8ff7f 5edbc37e ffff18ff c3ffffc3 feffc3c6 c3663cff 303ffff
  //   fff0f0ff ff3e7cff 7effc37e 78fccf7f 7fffcc78 73fecc7f 4edbdb72 c0ffffc0 fe0303fe fc0f0ffc
endmodule

module CharacterDisplayHandler (
  input  [4:0] CharacterPositionY,
  input  [4:0] Character,
  output [31:0] out_3,
  output [31:0] out_4,
  output [31:0] out_5,
  output [31:0] out_6
);

  wire [7:0] characterrom_1_out_2, characterrom_1_out_3, characterrom_1_out_4, characterrom_1_out_5;
  wire [31:0] bit_extender_1_out, bit_extender_2_out, bit_extender_3_out, bit_extender_4_out;

  CharacterROM characterrom_1 (
    .Character(Character), .out_2(characterrom_1_out_2), .out_3(characterrom_1_out_3),
    .out_4(characterrom_1_out_4), .out_5(characterrom_1_out_5));
  assign bit_extender_1_out = {{24{1'b0}}, characterrom_1_out_2};  // Bit_Extender bit_extender_1
  assign bit_extender_2_out = {{24{1'b0}}, characterrom_1_out_4};  // Bit_Extender bit_extender_2
  assign bit_extender_3_out = {{24{1'b0}}, characterrom_1_out_3};  // Bit_Extender bit_extender_3
  assign bit_extender_4_out = {{24{1'b0}}, characterrom_1_out_5};  // Bit_Extender bit_extender_4
  Shifter #(.width(32)) shifter_1 (.in(bit_extender_1_out), .\dist (CharacterPositionY), .out(out_3));
  Shifter #(.width(32)) shifter_2 (.in(bit_extender_3_out), .\dist (CharacterPositionY), .out(out_4));
  Shifter #(.width(32)) shifter_3 (.in(bit_extender_2_out), .\dist (CharacterPositionY), .out(out_5));
  Shifter #(.width(32)) shifter_4 (.in(bit_extender_4_out), .\dist (CharacterPositionY), .out(out_6));
endmodule

module PlayerHandler (
  input  Clock,
  input  IsComputerPlayer,
  input  LockMovement,
  input  ResetPaddleToCenter,
  input  [1:0] MovementDirection,
  input  [1:0] Difficulty,
  input  [4:0] PaddleSize,
  input  [7:0] BallY,
  output IsBallInPaddleRange,
  output [4:0] PaddlePositionY
);

  wire [1:0] computerenemymovementhandler_1_movement, multiplexer_1_out;
  wire [7:0] bit_extender_1_out;

  Multiplexer #(.width(2)) multiplexer_1 (
    .in0(MovementDirection), .in1(computerenemymovementhandler_1_movement), .out(multiplexer_1_out),
    .sel(IsComputerPlayer));
  PaddleHandler paddlehandler_1 (
    .LockMovement(LockMovement), .PaddleSize(PaddleSize), .ResetPosition(ResetPaddleToCenter), .Clock(Clock),
    .Direction(multiplexer_1_out), .BallY(BallY), .PaddlePositionY(PaddlePositionY),
    .IsInPaddleRange(IsBallInPaddleRange));
  ComputerEnemyMovementHandler computerenemymovementhandler_1 (
    .BallY(BallY), .PaddlePositionY(bit_extender_1_out), .Clock(Clock), .LockMovement(LockMovement),
    .Difficulty(Difficulty), .Movement(computerenemymovementhandler_1_movement));
  assign bit_extender_1_out = {{3{1'b0}}, PaddlePositionY};  // Bit_Extender bit_extender_1
endmodule

module BallCollisionHandler (
  input  [7:0] BallPositionX,
  input  CanCollideWithPlayerA,
  input  [7:0] PlayerAPositionX,
  input  CanCollideWithPlayerB,
  input  [7:0] PlayerBPositionX,
  input  [7:0] PlayfieldCenterX,
  output IsColliding,
  output IsOnLeftEdge,
  output IsOnRightEdge
);

  wire and_1_out, and_2_out, comparator_1_eq, comparator_2_eq;
  wire [7:0] adder_1_out, multiplier_1_out, subtractor_1_out;

  Adder adder_1 (.a(8'h1), .b(PlayerAPositionX), .out(adder_1_out));  // open: cin, cout
  Subtractor subtractor_1 (.a(PlayerBPositionX), .b(8'h1), .out(subtractor_1_out));  // open: bin, bout
  Multiplier multiplier_1 (.a(8'h2), .b(PlayfieldCenterX), .out(multiplier_1_out));  // open: cin, cout
  Comparator comparator_1 (.a(BallPositionX), .b(adder_1_out), .eq(comparator_1_eq), .lt(IsOnLeftEdge));  // open: gt
  Comparator comparator_2 (
    .a(BallPositionX), .b(subtractor_1_out), .gt(IsOnRightEdge), .eq(comparator_2_eq));  // open: lt
  Comparator comparator_3 (.a(BallPositionX), .b({8{1'b0}}));  // open: gt, eq, lt
  Comparator comparator_4 (.a(BallPositionX), .b(multiplier_1_out));  // open: gt, eq, lt
  and and_1 (and_1_out, comparator_1_eq, CanCollideWithPlayerA);
  and and_2 (and_2_out, CanCollideWithPlayerB, comparator_2_eq);
  or or_1 (IsColliding, and_1_out, and_2_out);
endmodule

module ScoreHandler (
  input  ClearScore,
  input  LockScore,
  input  Increment,
  output [15:0] Score
);

  wire not_1_out;

  not not_1 (not_1_out, LockScore);
  Counter #(.max('hffff), .ongoal("stay"), .width(16)) counter_1 (
    .clr(ClearScore), .load(1'b0), .up(1'b1), .count(not_1_out), .clk(Increment), .Q(Score));  // open: D, carry
endmodule

module BallStartDirectionHandler (
  input  [15:0] ScoreA,
  input  [15:0] ScoreB,
  input  Clock,
  input  IsNewGame,
  input  Reset,
  output [1:0] BallStartDirection
);

  wire comparator_1_eq, comparator_1_lt, t_ff_1_q;

  Comparator #(.mode("unsigned"), .width(16)) comparator_1 (
    .a(ScoreA), .b(ScoreB), .eq(comparator_1_eq), .lt(comparator_1_lt));  // open: gt
  T_Flip_Flop t_ff_1 (.T(Clock), .clk(IsNewGame), .Q(t_ff_1_q), .reset(Reset));  // open: Qn, preset
  T_Flip_Flop t_ff_2 (.T(Clock), .clk(Clock), .Q(BallStartDirection[1]), .reset(Reset));  // open: Qn, preset
  Multiplexer multiplexer_1 (.in0(comparator_1_lt), .in1(t_ff_1_q), .out(BallStartDirection[0]), .sel(comparator_1_eq));
endmodule

module PauseScreenHandler (
  input  Enable,
  input  [4:0] PausePositionY,
  input  [63:0] in_3,
  input  [63:0] in_4,
  input  [63:0] in_5,
  input  [63:0] in_6,
  input  [63:0] in_7,
  input  [63:0] in_8,
  input  [63:0] in_9,
  input  [63:0] in_10,
  input  [63:0] in_11,
  input  [63:0] in_12,
  input  [63:0] in_13,
  input  [63:0] in_14,
  output [63:0] out_15,
  output [63:0] out_16,
  output [63:0] out_17,
  output [63:0] out_18,
  output [63:0] out_19,
  output [63:0] out_20,
  output [63:0] out_21,
  output [63:0] out_22,
  output [63:0] out_23,
  output [63:0] out_24,
  output [63:0] out_25,
  output [63:0] out_26
);

  ToggleableCharacterHandler toggleablecharacterhandler_1 (
    .CharacterPositionY(PausePositionY), .Character(5'b11001), .in_3(in_3), .in_4(in_4), .Enabled(Enable),
    .out_6(out_15), .out_7(out_16));
  ToggleableCharacterHandler toggleablecharacterhandler_2 (
    .CharacterPositionY(PausePositionY), .Character(5'b01010), .in_3(in_5), .in_4(in_6), .Enabled(Enable),
    .out_6(out_17), .out_7(out_18));
  ToggleableCharacterHandler toggleablecharacterhandler_3 (
    .CharacterPositionY(PausePositionY), .Character(5'b11110), .in_3(in_7), .in_4(in_8), .Enabled(Enable),
    .out_6(out_19), .out_7(out_20));
  ToggleableCharacterHandler toggleablecharacterhandler_4 (
    .CharacterPositionY(PausePositionY), .Character(5'b11100), .in_3(in_9), .in_4(in_10), .Enabled(Enable),
    .out_6(out_21), .out_7(out_22));
  ToggleableCharacterHandler toggleablecharacterhandler_5 (
    .CharacterPositionY(PausePositionY), .Character(5'b01110), .in_3(in_11), .in_4(in_12), .Enabled(Enable),
    .out_6(out_23), .out_7(out_24));
  ToggleableCharacterHandler toggleablecharacterhandler_6 (
    .CharacterPositionY(PausePositionY), .Character(5'b01101), .in_3(in_13), .in_4(in_14), .Enabled(Enable),
    .out_6(out_25), .out_7(out_26));
endmodule

module ToggleableCharacterHandler (
  input  [4:0] CharacterPositionY,
  input  [4:0] Character,
  input  [63:0] in_3,
  input  [63:0] in_4,
  input  Enabled,
  output [63:0] out_6,
  output [63:0] out_7
);

  wire [4:0] adder_1_out;
  wire [31:0] and_1_out, and_2_out, and_3_out, and_4_out, characterdisplayhandler_1_out_3,
       characterdisplayhandler_1_out_4, characterdisplayhandler_1_out_5, characterdisplayhandler_1_out_6,
       not_1_out, or_1_out, or_2_out, or_3_out, or_4_out, shifter_1_out;

  Adder #(.width(5)) adder_1 (.a(5'b00001), .b(CharacterPositionY), .out(adder_1_out));  // open: cin, cout
  Shifter #(.width(32)) shifter_1 (.in(32'h3ff), .\dist (CharacterPositionY), .out(shifter_1_out));
  assign not_1_out = ~shifter_1_out;  // NOT_Gate not_1, 32 bits wide
  CharacterDisplayHandler characterdisplayhandler_1 (
    .CharacterPositionY(adder_1_out), .Character(Character), .out_3(characterdisplayhandler_1_out_3),
    .out_4(characterdisplayhandler_1_out_4), .out_5(characterdisplayhandler_1_out_5),
    .out_6(characterdisplayhandler_1_out_6));
  assign and_1_out = in_3[31:0] & not_1_out;  // AND_Gate and_1, 32 bits wide
  assign and_2_out = in_3[63:32] & not_1_out;  // AND_Gate and_2, 32 bits wide
  assign and_3_out = in_4[31:0] & not_1_out;  // AND_Gate and_3, 32 bits wide
  assign and_4_out = in_4[63:32] & not_1_out;  // AND_Gate and_4, 32 bits wide
  assign or_1_out = and_1_out | characterdisplayhandler_1_out_3;  // OR_Gate or_1, 32 bits wide
  assign or_2_out = and_2_out | characterdisplayhandler_1_out_4;  // OR_Gate or_2, 32 bits wide
  assign or_3_out = and_3_out | characterdisplayhandler_1_out_5;  // OR_Gate or_3, 32 bits wide
  assign or_4_out = and_4_out | characterdisplayhandler_1_out_6;  // OR_Gate or_4, 32 bits wide
  Multiplexer #(.width(64)) multiplexer_1 (.in0(in_3), .in1({or_2_out, or_1_out}), .out(out_6), .sel(Enabled));
  Multiplexer #(.width(64)) multiplexer_2 (.in0(in_4), .in1({or_4_out, or_3_out}), .out(out_7), .sel(Enabled));
endmodule
